# Fritzing sketch satellite_esp32 (saved by Fritzing 1.0.6)
breadboards: 1

parts:
  Part1 = BH1750
  A1 = GY-BMP280 Breakout
  A2 = ENS160 AHT21
  BAT1 = Battery Holders [package=lipo-1100mAh]
  D1 = SOLAR-IXYS [package=solarbit-12x1]
  D2 = SOLAR-IXYS [package=solarbit-12x1]
  WaveShare_1_3inch_OLED_128x2 = WaveShare 1.3inch OLED 128x64
  U1 = ESP32-38PinWide [part_number=ESP32-38PinWide]
  A3 = Solar charger SD05CRMA

nets:
  VCC: Part1.VCC, A1.Pin_1, A2.Pin_2, WaveShare_1_3inch_OLED_128x2.VCC, U1.3.3
  GND: Part1.GND, A1.Pin_2, A2.Pin_3, U1.GND
  N1: Part1.SCL, A1.Pin_3, A2.Pin_4, U1.GPIO22
  N2: Part1.SDA, A1.Pin_4, A2.Pin_5, U1.GPIO21
  N3: BAT1.+, A3.Pin_4
  N4: BAT1.-, D1.C, D2.C, A3.Pin_2, A3.Pin_3
  N5: D1.A, D2.A, A3.Pin_1
  N6: WaveShare_1_3inch_OLED_128x2.GND, U1.GPIO11
  N7: WaveShare_1_3inch_OLED_128x2.DIN, U1.GPIO13
  N8: WaveShare_1_3inch_OLED_128x2.CLK, U1.GPIO14
  N9: WaveShare_1_3inch_OLED_128x2.CS, U1.GPIO27
  N10: WaveShare_1_3inch_OLED_128x2.D/C, U1.GPIO26
  N11: WaveShare_1_3inch_OLED_128x2.RES, U1.GPIO25

custom parts:
  BH1750: Light Sensor
  ENS160 AHT21: The CO2 Gas- Air- Sensor is based on ENS160 in combination with an AHT21 Temperature Humidity Sensor.
  WaveShare 1.3inch OLED 128x64: OLED Original design by Simulz (http://tsblog.simulz.kr) Corrected PCB layout by Andreas Horneffer
  ESP32-38PinWide: Generic 38-Pin ESP32 with wide format (only access to one side of pins on a breadboard) based on Stephen Lilley's HiLetgo ESP-WROOM-32 ESP32 ESP-32S Development Board.
  Solar charger SD05CRMA: SD05CRMA 4.4-6.5V Input Solar Panel Dedicated Charging Module 18650 LiPo Li-ion Lithium Battery Charge Controller Module.
